# Fritzing sketch Fritzing Cuelight (saved by Fritzing 0.9.3b)
circuit board: 8.46667cm x 5.64444cm
breadboards: 2

parts:
  Part1 = Arduino Uno (Rev3) - ICSP
  LED2 = smd LED [color="Red (633nm)" package="0805 [SMD]"]
  LED3 = smd LED [color="Red (633nm)" package="0805 [SMD]"]
  S11 = Pushbutton [package=THT]
  S12 = Pushbutton [package=THT]
  S13 = Pushbutton [package=THT]
  S14 = Pushbutton [package=THT]
  S15 = Pushbutton [package=THT]
  LED1 = smd LED [color="Red (633nm)" package="0805 [SMD]"]

nets:
  N1: Part1.GND, LED2.cathode, LED3.cathode, S11.leg0, S12.leg0, S13.leg0, S14.leg0, S15.leg0, LED1.cathode
  N2: Part1.D8, LED3.anode
  N3: Part1.D9_PWM, LED2.anode
  N4: Part1.D10_PWM/SS, LED1.anode
  N5: Part1.D3_PWM, S11.leg1
  N6: Part1.D4, S12.leg1
  N7: Part1.D5_PWM, S13.leg1
  N8: Part1.D6_PWM, S14.leg1
  N9: Part1.D7, S15.leg1
